// Logisim project cpu.circ as structural Verilog
module main (
  input  [31:0] INSTRUCTION,
  input  CLOCK,
  output [31:0] FETCH_ADDRESS,
  output [31:0] ra_Value,
  output [31:0] sp_Value,
  output [31:0] t0_Value,
  output [31:0] t1_Value,
  output [31:0] t2_Value,
  output [31:0] s0_Value,
  output [31:0] s1_Value,
  output [31:0] a0_Value
);

  wire MEM_p2, MEM_p5, MEM_p8, MEM_p12, MEM_p15, MEM_p18;
  wire [4:0] instdecoder_1_inst_11_7, instdecoder_1_inst_19_15, instdecoder_1_inst_24_20;
  wire [24:0] instdecoder_1_inst_31_7;

  Multiplexer #(.width(32)) multiplexer_1 ();  // open: in0, in1, out, sel, en
  Register #(.width(32)) PC (.Q(FETCH_ADDRESS), .clk(CLOCK));  // open: D, en, clr
  plus_four plus_4 (.In(FETCH_ADDRESS));  // open: Out
  InstDecoder instdecoder_1 (
    .Instruction(INSTRUCTION), .inst_11_7(instdecoder_1_inst_11_7), .inst_19_15(instdecoder_1_inst_19_15),
    .inst_24_20(instdecoder_1_inst_24_20), .inst_31_7(instdecoder_1_inst_31_7));  // open: inst_31_0
  regfile_main main_1 (
    .Read_Register_1__rs1(instdecoder_1_inst_19_15), .Read_Register_2__rs2(instdecoder_1_inst_24_20),
    .Write_Register__rd(instdecoder_1_inst_11_7), .Clock(CLOCK));  // open: Write_Data, Write_Enable, Read_Data_1, Read_Data_2, ra_Value, sp_Value, t0_Value, t1_Value, t2_Value, s0_Value, s1_Value, a0_Value
  ImmGen immgen_1 (.inst_31_7(instdecoder_1_inst_31_7));  // open: ImmSel, imm_31_0
  // alu_main main_2: pin names not known
  // mem_main MEM: pin names not known; wires that end beside it: sp_Value, MEM_p2, MEM_p2, t0_Value, MEM_p5, MEM_p5, t1_Value, MEM_p8, CLOCK, MEM_p8, t2_Value, MEM_p12, MEM_p12, s0_Value, MEM_p15, MEM_p15, s1_Value, MEM_p18

  // Other names for the same wires on the sheet: clk = CLOCK; fetch_addr[31:0] = FETCH_ADDRESS

  // Notes on the sheet:
  //   Output
  //   These are outputs/inputs from run.circ
  //   Inputs
endmodule

module plus_four (
  input  [31:0] In,
  output [31:0] Out
);

  Adder #(.width(32)) adder_1 (.a(In), .b(32'h4), .out(Out));  // open: cin, cout
endmodule

module ImmGen (
  input  [24:0] inst_31_7,
  input  [2:0] ImmSel,
  output [31:0] imm_31_0
);

  wire [31:0] bit_extender_1_out, bit_extender_2_out, bit_extender_3_out, bit_extender_4_out,
       bit_extender_5_out, shifter_1_out;

  assign bit_extender_1_out = {{7{1'b0}}, inst_31_7};  // Bit_Extender bit_extender_1
  Shifter #(.width(32)) shifter_1 (.in(bit_extender_1_out), .\dist (5'b00111), .out(shifter_1_out));
  assign bit_extender_2_out = {{20{shifter_1_out[31]}}, shifter_1_out[31:20]};  // Bit_Extender bit_extender_2
  assign bit_extender_3_out = {{20{shifter_1_out[31]}}, {shifter_1_out[31:25], shifter_1_out[11:7]}};  // Bit_Extender bit_extender_3
  assign bit_extender_4_out = {{19{shifter_1_out[31]}}, {shifter_1_out[31], shifter_1_out[7], shifter_1_out[30:25], shifter_1_out[11:8], 1'b0}};  // Bit_Extender bit_extender_4
  assign bit_extender_5_out = {{11{shifter_1_out[31]}}, {shifter_1_out[31], shifter_1_out[19:12], shifter_1_out[20], shifter_1_out[30:21], 1'b0}};  // Bit_Extender bit_extender_5
  Multiplexer #(.select(3), .width(32)) multiplexer_1 (
    .in0(bit_extender_2_out), .in1(bit_extender_3_out), .in2(bit_extender_4_out),
    .in3({shifter_1_out[31:12], {12{1'b0}}}), .in4(bit_extender_5_out), .out(imm_31_0), .sel(ImmSel));  // open: in5, in6, in7, en

  // Notes on the sheet:
  //   I-Type
  //   S-Type
  //   B-Type
  //   U-Type
  //   J-Type
  //   0 = I-Type, 1 = S-Type, 2 = B-Type, 3 = U-Type, 4 = J-Type
endmodule

module BranchComp (
  input  [31:0] A,
  input  [31:0] B,
  input  BrUn,
  output BrEq,
  output BrLT
);

  wire comparator_1_eq, comparator_1_lt, comparator_2_eq, comparator_2_lt;

  Comparator #(.width(32), .mode("unsigned")) comparator_1 (
    .a(A), .b(B), .eq(comparator_1_eq), .lt(comparator_1_lt));  // open: gt
  Comparator #(.width(32)) comparator_2 (.a(A), .b(B), .eq(comparator_2_eq), .lt(comparator_2_lt));  // open: gt
  Multiplexer multiplexer_1 (.in0(comparator_2_eq), .in1(comparator_1_eq), .out(BrEq), .sel(BrUn));  // open: en
  Multiplexer multiplexer_2 (.in0(comparator_2_lt), .in1(comparator_1_lt), .out(BrLT), .sel(BrUn));  // open: en
endmodule

module InstDecoder (
  input  [31:0] Instruction,
  output [4:0] inst_11_7,
  output [4:0] inst_19_15,
  output [4:0] inst_24_20,
  output [24:0] inst_31_7,
  output [31:0] inst_31_0
);


  assign inst_11_7 = Instruction[11:7];
  assign inst_19_15 = Instruction[19:15];
  assign inst_24_20 = Instruction[24:20];
  assign inst_31_0 = Instruction;
  assign inst_31_7 = Instruction[31:7];
endmodule
