// Logisim project regfile.circ as structural Verilog: 1 circuit, main circuit main
module main (
  input  [4:0] Read_Register_1__rs1,
  input  [4:0] Read_Register_2__rs2,
  input  [4:0] Write_Register__rd,
  input  [31:0] Write_Data,
  input  Write_Enable,
  input  Clock,
  input  in_7,
  output [31:0] ra_Value,
  output [31:0] sp_Value,
  output [31:0] t0_Value,
  output [31:0] t1_Value,
  output [31:0] t2_Value,
  output [31:0] s0_Value,
  output [31:0] s1_Value,
  output [31:0] a0_Value,
  output [31:0] Read_Data_1,
  output [31:0] Read_Data_2
);

  wire write_a0, write_a1, write_ra, write_s0, write_s1, write_sp, write_t0, write_t1, write_t2, write_zero;

  Demultiplexer #(.select(5)) demultiplexer_1 (
    .out0(write_zero), .out1(write_ra), .out2(write_sp), .out5(write_t0), .out6(write_t1), .out7(write_t2),
    .out8(write_s0), .out9(write_s1), .out10(write_a0), .out11(write_a1), .in(in_7), .sel(Write_Register__rd));  // open: out3, out4, out12, out13, out14, out15, out16, out17, out18, out19, out20, out21, out22, out23, out24, out25, out26, out27, out28, out29, out30, out31, en

  // Other names for the same wires on the sheet: clk = Clock; read_data1[31:0] = Read_Data_1;
  //   read_data2[31:0] = Read_Data_2; read_reg1[4:0] = Read_Register_1__rs1; read_reg2[4:0] = Read_Register_2__rs2;
  //   write_en = Write_Enable; write_reg[4:0] = Write_Register__rd

  // Notes on the sheet:
  //   INPUTS to your circuit
  //   These are DEBUG/TEST outputs from your circuit.
  //   DON'T CHANGE THE LOCATIONS OF THE INPUTS AND OUTPUTS!
  //   OUTPUTS from your circuit
endmodule
